# Fritzing sketch Schematic_uno (saved by Fritzing 0.9.6b)
breadboards: 2

parts:
  Part1 = Arduino Uno (Rev3)
  R1 = Trimmer Potentiometer [maximum_resistance=10kΩ package=THT]
  Volume = Pushbutton [package="[SMD]"]
  Volume_2 = Pushbutton [package="[THT]"]
  RE1 = Rotary Encoder [package=THT]
  Part2 = Digital FM Radio Receiver
  U2 = LCD-16X2 [package=lcd-16x2_noholes]
  R2 = Resistor [tolerance=±5% resistance=220 package="1206 [SMD]"]
  Reset = Pushbutton [package="[THT]"]
  C1 = Capacitor [package=cap-pth-small2]
  C2 = Capacitor [package=cap-pth-small2]
  Mute = Momentary Switch [package=ksa_sealed_tac_switch]
  LED1 = LEDs [package=led10mm]
  R3 = Resistor [tolerance=±5% resistance=220 package="1206 [SMD]"]
  Power_button = SWITCH-SPST-2 [package=switch-spst-vertical]
  R4 = Resistor [tolerance=±5% resistance=220 package="1206 [SMD]"]

nets:
  N1: Part1.A0, R3.Pin_1
  N2: Part1.A1, RE1.EncoderPinB
  N3: Part1.A2, RE1.EncoderPinA
  GND: Part1.A3, Part1.GND, R1.leg1, Volume.Pin_3, Volume.Pin_4, Volume_2.Pin_3, Volume_2.Pin_4, Part2.GND, U2.VSS, U2.R_W, U2.K, Reset.Pin_3, Reset.Pin_4, C1.1, C2.1, Mute.3, Power_button.P, R4.Pin_0, R4.Pin_1
  N4: Part1.A4/SDA, Part2.SDIO
  N5: Part1.A5/SCL, Part2.SCLK
  N6: Part1.D8, Volume_2.Pin_1, Volume_2.Pin_2, C1.2
  N7: Part1.D9_PWM, Volume.Pin_1, Volume.Pin_2, C2.2
  N8: Part1.D10_PWM/SS, Mute.1
  N9: Part1.D11_PWM/MOSI, U2.E
  N10: Part1.D12/MISO, U2.RS
  N11: Part1.D2, Part2.!RST
  N12: Part1.D3_PWM, Part2.!SEN
  N13: Part1.D4, U2.DB6
  N14: Part1.D5_PWM, U2.DB5
  N15: Part1.D6_PWM, U2.DB4
  N16: Part1.D7, U2.DB7
  N17: Part1.RESET, Reset.Pin_1, Reset.Pin_2
  3V3: Part1.3V3, Part2.3.3V
  5V: Part1.5V, R1.leg2, RE1.EncoderPinC, U2.VDD, R2.Pin_0, Power_button.O
  N18: R1.wiper, U2.VO
  N19: U2.A, R2.Pin_1
  N20: LED1.A, R3.Pin_0

notes:
  Volume, reset & mute buttons
